// Digital circuit ALU.dig as structural Verilog
module ALU (
  input  [2:0] F,
  input  [31:0] A,
  input  [31:0] B,
  output _0,
  output [31:0] Y
);

  wire [0:0] comparator_1_lt;
  wire [31:0] add_1_s, and_1_out, multiplexer_1_out, not_1_out, or_1_out;

  assign not_1_out = ~B;  // Not not_1, 32 bits wide
  Multiplexer #(.Bits(32)) multiplexer_1 (.sel(F[2]), .in_0(B), .in_1(not_1_out), .out(multiplexer_1_out));
  assign and_1_out = A & multiplexer_1_out;  // And and_1, 32 bits wide
  assign or_1_out = A | multiplexer_1_out;  // Or or_1, 32 bits wide
  Add #(.Bits(32)) add_1 (.a(A), .b(multiplexer_1_out), .c_i(F[2]), .s(add_1_s));  // open: c_o
  Comparator #(.Signed("true"), .Bits(32)) comparator_1 (.a(A), .b(B), .lt(comparator_1_lt[0]));  // open: gt, eq
  Multiplexer #(.Selector_Bits(2), .Bits(32)) multiplexer_2 (
    .sel(F[1:0]), .in_0(and_1_out), .in_1(or_1_out), .in_2(add_1_s), .in_3({{31{1'b0}}, comparator_1_lt[0]}),
    .out(Y));
  Comparator #(.Bits(32)) comparator_2 (.a({32{1'b0}}), .b(Y), .eq(_0));  // open: gt, lt

  // Other names for the same wires on the sheet: F1_0[1:0] = F[1:0]
endmodule
