// Digital circuit ALUDecoder.dig as structural Verilog
module ALUDecoder (
  input  [1:0] ALUOp,
  input  [5:0] Funct,
  output [2:0] ALUControl
);

  wire and_1_out, and_2_out, and_3_out, and_4_out, not_1_out, not_2_out, not_3_out, not_4_out, not_5_out,
       not_6_out, not_7_out, or_1_out, or_2_out;

  not not_1 (not_1_out, ALUOp[1]);
  not not_2 (not_2_out, Funct[0]);
  not not_3 (not_3_out, Funct[1]);
  not not_4 (not_4_out, Funct[2]);
  not not_5 (not_5_out, Funct[3]);
  not not_6 (not_6_out, Funct[4]);
  not not_7 (not_7_out, Funct[5]);
  and and_1 (and_1_out, ALUOp[1], not_2_out, Funct[1], not_4_out, not_5_out, not_6_out, Funct[5]);
  and and_2 (and_2_out, ALUOp[1], not_2_out, Funct[1], not_4_out, Funct[3], not_6_out, Funct[5]);
  or or_1 (or_1_out, not_1_out, Funct[0], Funct[1], not_4_out, Funct[3], Funct[4], not_7_out);
  or or_2 (or_2_out, not_1_out, not_2_out, Funct[1], not_4_out, Funct[3], Funct[4], not_7_out);
  and and_3 (and_3_out, ALUOp[1], Funct[0], not_3_out, Funct[2], not_5_out, not_6_out, Funct[5]);
  and and_4 (and_4_out, ALUOp[1], not_2_out, Funct[1], not_4_out, Funct[3], not_6_out, Funct[5]);
  or or_3 (ALUControl[2], ALUOp[0], and_1_out, and_2_out);
  and and_5 (ALUControl[1], or_1_out, or_2_out);
  or or_4 (ALUControl[0], and_3_out, and_4_out);

  // Other names for the same wires on the sheet: ac0 = ALUControl[0]; ac1 = ALUControl[1]; ac2 = ALUControl[2];
  //   ao0 = ALUOp[0]; ao1 = ALUOp[1]; f0 = Funct[0]; f1 = Funct[1]; f2 = Funct[2]; f3 = Funct[3]; f4 = Funct[4];
  //   f5 = Funct[5]
endmodule
