// Digital circuit MultiCycleControlUnit.dig as structural Verilog
module MultiCycleControlUnit (
  input  clk,
  input  [5:0] Op,
  input  [5:0] Funct,
  output MemtoReg,
  output RegDst,
  output IorD,
  output [1:0] PCSrc,
  output [1:0] ALUSrcB,
  output ALUSrcA,
  output IRWrite,
  output MemWrite,
  output PCWrite,
  output Branch,
  output RegWrite,
  output [2:0] ALUControl
);

  wire [1:0] multicyclemaincontrol_1_aluop;

  MultiCycleMainControl multicyclemaincontrol_1 (
    .C(clk), .Op(Op), .MemtoReg(MemtoReg), .RegDst(RegDst), .IorD(IorD), .PCSrc(PCSrc), .ALUSrcB(ALUSrcB),
    .ALUSrcA(ALUSrcA), .IRWirte(IRWrite), .MemWrite(MemWrite), .PCWrite(PCWrite), .Branch(Branch),
    .RegWrite(RegWrite), .ALUOp(multicyclemaincontrol_1_aluop));
  ALUDecoder aludecoder_1 (.ALUOp(multicyclemaincontrol_1_aluop), .Funct(Funct), .ALUControl(ALUControl));
  // Pins of 1 and 3 bits meet at ALUControl
  // Pins of 1 and 2 bits meet at PCSrc
  // Pins of 1 and 2 bits meet at ALUSrcB
endmodule
