// Digital circuit MultiCycleMainControl.dig as structural Verilog
module MultiCycleMainControl (
  input  C,
  input  [5:0] Op,
  output MemtoReg,
  output RegDst,
  output IorD,
  output [1:0] PCSrc,
  output [1:0] ALUSrcB,
  output ALUSrcA,
  output IRWirte,
  output MemWrite,
  output PCWrite,
  output Branch,
  output RegWrite,
  output [1:0] ALUOp
);

  wire and_1_out, and_2_out, and_3_out, and_4_out, and_5_out, and_6_out, and_7_out, and_8_out, and_9_out,
       and_10_out, and_11_out, and_12_out, and_13_out, and_14_out, and_15_out, and_16_out, and_17_out,
       and_18_out, and_19_out, and_20_out, and_21_out, and_22_out, and_23_out, and_24_out, and_25_out,
       and_26_out, and_27_out, and_30_out, and_31_out, and_33_out, and_34_out, and_37_out, and_38_out,
       and_43_out, and_44_out, and_46_out, and_47_out, and_48_out, not_1_out, not_2_out, not_3_out,
       not_4_out, not_5_out, not_6_out, not_7_out, not_8_out, not_9_out, not_10_out, or_1_out, or_2_out,
       or_8_out, or_9_out, Z_0_n, Z_1_n, Z_2_n, Z_3_n;

  not not_1 (not_1_out, Op[0]);
  not not_2 (not_2_out, Op[1]);
  not not_3 (not_3_out, Op[2]);
  not not_4 (not_4_out, Op[3]);
  not not_5 (not_5_out, Op[4]);
  not not_6 (not_6_out, Op[5]);
  not not_7 (not_7_out, Z_3_n);
  not not_8 (not_8_out, Z_2_n);
  not not_9 (not_9_out, Z_1_n);
  not not_10 (not_10_out, Z_0_n);
  and and_1 (and_1_out, Z_0_n, not_9_out, not_8_out, not_1_out, not_2_out, not_3_out, Op[3], not_5_out, not_6_out);
  and and_2 (and_2_out, Z_0_n, not_9_out, not_8_out, not_1_out, not_2_out, Op[2], not_4_out, not_5_out, not_6_out);
  and and_3 (and_3_out, Z_0_n, not_9_out, not_8_out, not_1_out, Op[1], not_3_out, not_4_out, not_5_out, not_6_out);
  and and_4 (and_4_out, Z_0_n, not_9_out, Z_3_n);
  and and_5 (and_5_out, not_10_out, Z_1_n, not_7_out, Op[0], Op[1], not_3_out, Op[3], not_5_out, Op[5]);
  and and_6 (and_6_out, Z_0_n, not_8_out, not_7_out, not_1_out, not_2_out, not_3_out, not_4_out, not_5_out, not_6_out);
  and and_7 (and_7_out, Z_0_n, Z_1_n, not_8_out, not_7_out);
  and and_8 (and_8_out, not_10_out, Z_1_n, Z_2_n);
  and and_9 (and_9_out, Z_0_n, not_9_out, not_8_out, not_1_out, not_3_out, not_4_out, not_5_out, not_6_out);
  and and_10 (and_10_out, Z_0_n, not_9_out, not_8_out, Op[0], Op[1], not_3_out, not_5_out, Op[5]);
  and and_11 (and_11_out, not_10_out, Z_1_n, not_7_out, not_6_out);
  and and_12 (and_12_out, not_10_out, Z_1_n, not_7_out, Op[4]);
  and and_13 (and_13_out, not_10_out, Z_1_n, not_7_out, not_4_out);
  and and_14 (and_14_out, not_10_out, Z_1_n, not_7_out, Op[2]);
  and and_15 (and_15_out, not_10_out, Z_1_n, not_7_out, not_2_out);
  and and_16 (and_16_out, not_10_out, Z_1_n, not_7_out, not_1_out);
  and and_17 (and_17_out, not_10_out, Z_1_n, Z_2_n);
  and and_18 (and_18_out, Z_0_n, not_9_out, Z_3_n);
  and and_19 (and_19_out, not_10_out, Z_1_n, not_7_out, Op[0], Op[1], not_3_out, not_5_out, Op[5]);
  and and_20 (and_20_out, not_10_out, not_9_out, not_8_out, not_7_out);
  and and_21 (and_21_out, not_10_out, Z_1_n, Z_2_n);
  and and_22 (and_22_out, not_9_out, not_8_out, not_7_out, Op[3], not_6_out);
  and and_23 (and_23_out, not_9_out, not_8_out, not_7_out, Op[2], Op[5]);
  and and_24 (and_24_out, not_9_out, not_8_out, not_7_out, not_2_out, Op[5]);
  and and_25 (and_25_out, not_9_out, not_8_out, not_7_out, Op[0], not_6_out);
  and and_26 (and_26_out, not_9_out, not_8_out, not_7_out, not_1_out, Op[1]);
  and and_27 (and_27_out, not_9_out, not_8_out, not_7_out, Op[4]);
  and and_28 (ALUOp[0], not_10_out, not_9_out, Z_3_n);
  and and_29 (ALUOp[1], not_10_out, Z_1_n, Z_2_n);
  and and_30 (and_30_out, not_10_out, Z_1_n, not_7_out);
  and and_31 (and_31_out, not_9_out, Z_3_n);
  and and_32 (ALUSrcB[0], not_9_out, not_8_out, not_7_out);
  and and_33 (and_33_out, Z_0_n, not_9_out, not_8_out);
  and and_34 (and_34_out, not_10_out, Z_1_n, not_8_out, not_7_out);
  and and_35 (Branch, not_10_out, not_9_out, Z_3_n);
  and and_36 (IRWirte, not_10_out, not_9_out, not_8_out, not_7_out);
  and and_37 (and_37_out, Z_0_n, Z_1_n, not_8_out, not_7_out);
  and and_38 (and_38_out, Z_0_n, not_9_out, Z_2_n);
  and and_39 (MemWrite, Z_0_n, not_9_out, Z_2_n);
  and and_40 (MemtoReg, not_10_out, not_9_out, Z_2_n);
  and and_41 (PCSrc[0], not_10_out, not_9_out, Z_3_n);
  and and_42 (PCSrc[1], Z_0_n, Z_1_n, Z_3_n);
  and and_43 (and_43_out, not_10_out, not_9_out, not_8_out, not_7_out);
  and and_44 (and_44_out, Z_0_n, Z_1_n, Z_3_n);
  and and_45 (RegDst, Z_0_n, Z_1_n, Z_2_n);
  and and_46 (and_46_out, not_10_out, not_9_out, Z_2_n);
  and and_47 (and_47_out, Z_0_n, Z_1_n, Z_2_n);
  and and_48 (and_48_out, not_10_out, Z_1_n, Z_3_n);
  or or_1 (or_1_out, and_1_out, and_2_out, and_3_out, and_4_out);
  or or_2 (or_2_out, and_5_out, and_6_out, and_7_out, and_8_out);
  or or_3 (ALUSrcA, and_30_out, and_31_out);
  or or_4 (ALUSrcB[1], and_33_out, and_34_out);
  or or_5 (IorD, and_37_out, and_38_out);
  or or_6 (PCWrite, and_43_out, and_44_out);
  or or_7 (RegWrite, and_46_out, and_47_out, and_48_out);
  or or_8 (or_8_out, and_9_out, and_10_out, and_11_out, and_12_out, and_13_out, and_14_out, and_15_out, and_16_out, and_17_out, and_18_out);
  or or_9 (or_9_out, and_19_out, and_20_out, and_21_out, and_22_out, and_23_out, and_24_out, and_25_out, and_26_out, and_27_out);
  D_FF u_Z_3_n (.D(or_1_out), .C(C), .Q(Z_3_n));  // open: nQ
  D_FF u_Z_2_n (.D(or_2_out), .C(C), .Q(Z_2_n));  // open: nQ
  D_FF u_Z_1_n (.D(or_8_out), .C(C), .Q(Z_1_n));  // open: nQ
  D_FF u_Z_0_n (.D(or_9_out), .C(C), .Q(Z_0_n));  // open: nQ
  // Probe MultiCycleMainControlFSM.fsm on {Z_3_n, Z_2_n, Z_1_n, Z_0_n}

  // Other names for the same wires on the sheet: o0 = Op[0]; o1 = Op[1]; o2 = Op[2]; o3 = Op[3]; o4 = Op[4];
  //   o5 = Op[5]

  // Notes on the sheet:
  //   C: Hz: 2
endmodule
