// Digital circuit MultiCycleProcessor.dig as structural Verilog
module MultiCycleProcessor (
  input  clk
);

  wire alu_1_p4, ALUControl, ALUSrcA, and_1_out, Branch, IorD, IRWrite, MemtoReg, MemWrite, PCEn, PCWrite,
       RegDst, RegWrite;
  wire [1:0] ALUSrcB, PCSrc;
  wire [4:0] I10_6, I20_16, multiplexer_2_out;
  wire [5:0] I5_0, I31_26;
  wire [15:11] I15_0;
  wire [25:21] I25_0;
  wire [31:0] alu_1_p5, ALUOut, barrelshifter_1_out, bitextender_1_out, Data, Db, div_1_q, Memory_d,
       multiplexer_1_out, multiplexer_3_out, multiplexer_4_out, multiplexer_5_out, PCCur, PCNext,
       register_3_q, registerfile_1_da, registerfile_1_db;

  Register #(.Bits(32)) PC (.D(PCNext), .C(clk), .en(PCEn), .Q(PCCur));
  // Probe on PCCur
  Multiplexer #(.Bits(32)) multiplexer_1 (.sel(IorD), .in_0(PCCur), .in_1(ALUOut), .out(multiplexer_1_out));
  Div #(.Bits(32)) div_1 (.a(multiplexer_1_out), .b(32'h4), .q(div_1_q));  // open: r
  EEPROMDualPort #(.AddrBits(16), .Bits(32)) Memory (
    .A(div_1_q[15:0]), .Din(Db), .str(MemWrite), .C(clk), .ld(1'b1), .D(Memory_d));
  Register #(.Bits(32)) register_1 (
    .D(Memory_d), .C(clk), .en(IRWrite), .Q({I31_26, I25_0, I20_16, I15_0, I10_6, I5_0}));
  Register #(.Bits(32)) register_2 (.D(Memory_d), .C(clk), .en(1'b1), .Q(Data));
  // MultiCycleControlUnit multicyclecontrolunit_1: pin names not known; wires that end beside it: clk, I31_26, I5_0, MemtoReg, RegDst, IorD, PCSrc, ALUSrcB, ALUSrcA, IRWrite, MemWrite, PCWrite, Branch, RegWrite, ALUControl
  // Probe on {I31_26, I25_0, I20_16, I15_0, I10_6, I5_0}
  Multiplexer #(.Bits(5)) multiplexer_2 (.sel(RegDst), .in_0(I20_16), .in_1(I15_0), .out(multiplexer_2_out));
  Multiplexer #(.Bits(32)) multiplexer_3 (.sel(MemtoReg), .in_0(ALUOut), .in_1(Data), .out(multiplexer_3_out));
  RegisterFile #(.AddrBits(5), .Bits(32)) registerfile_1 (
    .Din(multiplexer_3_out), .we(RegWrite), .Rw(multiplexer_2_out), .C(clk), .Ra(I25_0), .Rb(I20_16),
    .Da(registerfile_1_da), .Db(registerfile_1_db));
  Register #(.Bits(32)) register_3 (.D(registerfile_1_da), .C(clk), .en(1'b1), .Q(register_3_q));
  Register #(.Bits(32)) register_4 (.D(registerfile_1_db), .C(clk), .en(1'b1), .Q(Db));
  BitExtender #(.inputBits(16), .outputBits(32)) bitextender_1 (.in({I15_0, I10_6, I5_0}), .out(bitextender_1_out));
  Multiplexer #(.Bits(32)) multiplexer_4 (.sel(ALUSrcA), .in_0(PCCur), .in_1(register_3_q), .out(multiplexer_4_out));
  BarrelShifter #(.Bits(32)) barrelshifter_1 (.in(bitextender_1_out), .shift(6'b000010), .out(barrelshifter_1_out));
  Multiplexer #(.Selector_Bits(2), .Bits(32)) multiplexer_5 (
    .sel(ALUSrcB), .in_0(Db), .in_1(32'h4), .in_2(bitextender_1_out), .in_3(barrelshifter_1_out),
    .out(multiplexer_5_out));
  // ALU alu_1: pin names not known; wires that end beside it: ALUControl, multiplexer_4_out, multiplexer_5_out, alu_1_p4, alu_1_p5
  and and_1 (and_1_out, Branch, alu_1_p4);
  Register #(.Bits(32)) register_5 (.D(alu_1_p5), .C(clk), .en(1'b1), .Q(ALUOut));
  or or_1 (PCEn, PCWrite, and_1_out);
  Multiplexer #(.Selector_Bits(2), .Bits(32)) multiplexer_6 (
    .sel(PCSrc), .in_0(alu_1_p5), .in_1(ALUOut),
    .in_2({PCCur[31:28], I25_0, I20_16, I15_0, I10_6, I5_0, 2'b00}), .in_3({32{1'b0}}), .out(PCNext));

  // Other names for the same wires on the sheet: I15_0[10:0] = {I10_6, I5_0};
  //   I25_0[20:0] = {I20_16, I15_0, I10_6, I5_0}; I15_11[4:0] = I15_0; I25_21[4:0] = I25_0

  // Notes on the sheet:
  //   clk: Hz: 10
  //   contents of Memory (hex, n*v repeats v):
  //   ac000064,ac000068,20020005,2003000c,2067fff7,e22025,642824,a42820,10a7000a,64202a,
  //   10800001,20050000,e2202a,853820,e23822,ac670058,8c020064,8000013,20020001,ac020068,
  //   8000014
  //   funct 5:0
  //   shamt 10:6
  //   rd 15:11
  //   rt 20:16
  //   rs 25:21
  //   op 31:26
endmodule
