// Digital circuit HazardUnit.dig as structural Verilog
module HazardUnit (
  input  [4:0] rsD,
  input  [4:0] rtD,
  input  [4:0] rsE,
  input  [4:0] rtE,
  input  [4:0] WriteRegE,
  input  [4:0] WriteRegM,
  input  [4:0] WriteRegW,
  input  BranchD,
  input  RegWriteE,
  input  MemtoRegE,
  input  RegWriteM,
  input  MemtoRegM,
  input  RegWriteW,
  output ForwardAD,
  output ForwardBD,
  output [1:0] ForwardAE,
  output [1:0] ForwardBE,
  output StallF,
  output StallD,
  output FlushE
);

  wire and_1_out, and_2_out, and_3_out, and_4_out, and_8_out, and_9_out, branchstall, comparator_1_eq,
       comparator_2_eq, comparator_3_eq, comparator_4_eq, comparator_5_eq, comparator_6_eq, comparator_7_eq,
       comparator_8_eq, comparator_9_eq, comparator_10_eq, comparator_11_eq, comparator_12_eq,
       comparator_13_eq, comparator_14_eq, comparator_15_eq, comparator_16_eq, comparator_17_eq,
       comparator_18_eq, lwstall, not_1_out, not_2_out, not_3_out, not_4_out, not_5_out, not_6_out, or_1_out,
       or_2_out, or_3_out;

  Comparator #(.Bits(5)) comparator_1 (.a(rsE), .b({5{1'b0}}), .eq(comparator_1_eq));  // open: gt, lt
  Comparator #(.Bits(5)) comparator_2 (.a(rsE), .b(WriteRegW), .eq(comparator_2_eq));  // open: gt, lt
  Comparator #(.Bits(5)) comparator_3 (.a(rsE), .b({5{1'b0}}), .eq(comparator_3_eq));  // open: gt, lt
  Comparator #(.Bits(5)) comparator_4 (.a(rsE), .b(WriteRegM), .eq(comparator_4_eq));  // open: gt, lt
  Comparator #(.Bits(5)) comparator_5 (.a(rtE), .b({5{1'b0}}), .eq(comparator_5_eq));  // open: gt, lt
  Comparator #(.Bits(5)) comparator_6 (.a(rtE), .b(WriteRegW), .eq(comparator_6_eq));  // open: gt, lt
  Comparator #(.Bits(5)) comparator_7 (.a(rtE), .b({5{1'b0}}), .eq(comparator_7_eq));  // open: gt, lt
  Comparator #(.Bits(5)) comparator_8 (.a(rtE), .b(WriteRegM), .eq(comparator_8_eq));  // open: gt, lt
  not not_1 (not_1_out, comparator_1_eq);
  not not_2 (not_2_out, comparator_3_eq);
  not not_3 (not_3_out, comparator_5_eq);
  not not_4 (not_4_out, comparator_7_eq);
  and and_1 (and_1_out, not_1_out, comparator_2_eq, RegWriteW);
  and and_2 (and_2_out, not_2_out, comparator_4_eq, RegWriteM);
  and and_3 (and_3_out, not_3_out, comparator_6_eq, RegWriteW);
  and and_4 (and_4_out, not_4_out, comparator_8_eq, RegWriteM);
  LookUpTable #(.Bits(2)) lookuptable_1 (.in0(and_1_out), .in1(and_2_out), .out(ForwardAE));
  LookUpTable #(.Bits(2)) lookuptable_2 (.in0(and_3_out), .in1(and_4_out), .out(ForwardBE));
  Comparator #(.Bits(5)) comparator_9 (.a(rsD), .b({5{1'b0}}), .eq(comparator_9_eq));  // open: gt, lt
  Comparator #(.Bits(5)) comparator_10 (.a(rsD), .b(WriteRegM), .eq(comparator_10_eq));  // open: gt, lt
  Comparator #(.Bits(5)) comparator_11 (.a(rtD), .b({5{1'b0}}), .eq(comparator_11_eq));  // open: gt, lt
  Comparator #(.Bits(5)) comparator_12 (.a(rtD), .b(WriteRegM), .eq(comparator_12_eq));  // open: gt, lt
  not not_5 (not_5_out, comparator_9_eq);
  not not_6 (not_6_out, comparator_11_eq);
  and and_5 (ForwardAD, not_5_out, comparator_10_eq, RegWriteM);
  and and_6 (ForwardBD, not_6_out, comparator_12_eq, RegWriteM);
  Comparator #(.Bits(5)) comparator_13 (.a(rsD), .b(rtE), .eq(comparator_13_eq));  // open: gt, lt
  Comparator #(.Bits(5)) comparator_14 (.a(rtD), .b(rtE), .eq(comparator_14_eq));  // open: gt, lt
  Comparator #(.Bits(5)) comparator_15 (.a(WriteRegE), .b(rsD), .eq(comparator_15_eq));  // open: gt, lt
  Comparator #(.Bits(5)) comparator_16 (.a(WriteRegE), .b(rtD), .eq(comparator_16_eq));  // open: gt, lt
  Comparator #(.Bits(5)) comparator_17 (.a(WriteRegM), .b(rsD), .eq(comparator_17_eq));  // open: gt, lt
  Comparator #(.Bits(5)) comparator_18 (.a(WriteRegM), .b(rtD), .eq(comparator_18_eq));  // open: gt, lt
  or or_1 (or_1_out, comparator_15_eq, comparator_16_eq);
  or or_2 (or_2_out, comparator_17_eq, comparator_18_eq);
  or or_3 (or_3_out, comparator_13_eq, comparator_14_eq);
  and and_7 (lwstall, or_3_out, MemtoRegE);
  and and_8 (and_8_out, BranchD, RegWriteE, or_1_out);
  and and_9 (and_9_out, BranchD, MemtoRegM, or_2_out);
  or or_4 (branchstall, and_8_out, and_9_out);
  or or_5 (FlushE, lwstall, branchstall);

  assign StallD = FlushE;
  assign StallF = FlushE;

  // Other names for the same wires on the sheet: BD = BranchD; FAD = ForwardAD; FAE[1:0] = ForwardAE; FBD = ForwardBD;
  //   FBE[1:0] = ForwardBE; MRE = MemtoRegE; MRM = MemtoRegM; RWE = RegWriteE; RWM = RegWriteM; RWW = RegWriteW;
  //   F = FlushE; SD = FlushE; SF = FlushE; WRE[4:0] = WriteRegE; WRM[4:0] = WriteRegM; WRW[4:0] = WriteRegW

  // Notes on the sheet:
  //   contents of lookuptable_1 (hex, n*v repeats v):
  //   0,1,2,2
  //   contents of lookuptable_2 (hex, n*v repeats v):
  //   0,1,2,2
endmodule
