// Digital circuit HazardUnitVerilog.dig as structural Verilog
module HazardUnitVerilog (
  input  [4:0] rsD,
  input  [4:0] rtD,
  input  [4:0] rsE,
  input  [4:0] rtE,
  input  [4:0] WriteRegE,
  input  [4:0] WriteRegM,
  input  [4:0] WriteRegW,
  input  BranchD,
  input  RegWriteE,
  input  MemtoRegE,
  input  RegWriteM,
  input  MemtoRegM,
  input  RegWriteW,
  output ForwardAD,
  output ForwardBD,
  output [1:0] ForwardAE,
  output [1:0] ForwardBE,
  output StallF,
  output StallD,
  output FlushE
);

  HazardUnit #(.applicationType("IVERILOG")) u_HazardUnit (
    .rsD(rsD), .rtD(rtD), .rsE(rsE), .rtE(rtE), .WriteRegE(WriteRegE), .WriteRegM(WriteRegM),
    .WriteRegW(WriteRegW), .BranchD(BranchD), .RegWriteE(RegWriteE), .MemtoRegE(MemtoRegE),
    .RegWriteM(RegWriteM), .MemtoRegM(MemtoRegM), .RegWriteW(RegWriteW), .ForwardAD(ForwardAD),
    .ForwardBD(ForwardBD), .ForwardAE(ForwardAE), .ForwardBE(ForwardBE), .StallF(StallF), .StallD(StallD),
    .FlushE(FlushE));
endmodule

/* Code of HazardUnit:
module HazardUnit(rsD,rtD,rsE,rtE,WriteRegE,WriteRegM,WriteRegW,
        BranchD,RegWriteE,MemtoRegE,RegWriteM,MemtoRegM,RegWriteW,
        ForwardAD,ForwardBD,ForwardAE,ForwardBE,
        StallF,StallD,FlushE);
    input [4:0] rsD,rtD,rsE,rtE,WriteRegE,WriteRegM,WriteRegW;
    input BranchD,RegWriteE,MemtoRegE,RegWriteM,MemtoRegM,RegWriteW;
    output ForwardAD,ForwardBD;
    output reg [1:0] ForwardAE,ForwardBE;
    output StallF,StallD,FlushE;

    always @* begin
        if( (rsE!=0) && (rsE==WriteRegM) && RegWriteM )
            ForwardAE=2'b10;
        else if( (rsE!=0) && (rsE==WriteRegW) && RegWriteW )
            ForwardAE=2'b01;
        else
            ForwardAE=2'b00;

        if( (rtE!=0) && (rtE==WriteRegM) && RegWriteM )
            ForwardBE=2'b10;
        else if( (rtE!=0) && (rtE==WriteRegW) && RegWriteW )
            ForwardBE=2'b01;
        else
            ForwardBE=2'b00;
    end
    
    assign ForwardAD=(rsD!=0) && (rsD==WriteRegM) && RegWriteM;
    assign ForwardBD=(rtD!=0) && (rtD==WriteRegM) && RegWriteM;

    assign lwstall=( ( (rsD==rtE) || (rtD==rtE) ) && MemtoRegE );
    assign branchstall=(BranchD && RegWriteE && ( (WriteRegE==rsD) || (WriteRegE==rtD) ) ) ||
        (BranchD && MemtoRegM && ( (WriteRegM==rsD) || (WriteRegM==rtD) ) );

    assign StallF=lwstall || branchstall;
    assign StallD=lwstall || branchstall;
    assign FlushE=lwstall || branchstall;
endmodule
*/
