// Digital circuit PipelinedControlUnit.dig as structural Verilog
module PipelinedControlUnit (
  input  [5:0] Op,
  input  [5:0] Funct,
  output RegWriteD,
  output MemtoRegD,
  output MemWriteD,
  output [2:0] ALUControlD,
  output ALUSrcD,
  output RegDstD,
  output BranchD,
  output JumpD
);

  wire [1:0] singlecyclemaindecoder_1_aluop;

  SingleCycleMainDecoder singlecyclemaindecoder_1 (
    .Op(Op), .MemtoReg(MemtoRegD), .MemWrite(MemWriteD), .Branch(BranchD), .ALUSrc(ALUSrcD),
    .RegDst(RegDstD), .RegWrite(RegWriteD), .Jump(JumpD), .ALUOp(singlecyclemaindecoder_1_aluop));
  ALUDecoder aludecoder_1 (.ALUOp(singlecyclemaindecoder_1_aluop), .Funct(Funct), .ALUControl(ALUControlD));

  // Other names for the same wires on the sheet: as = ALUSrcD; b = BranchD; j = JumpD; mr = MemtoRegD; mw = MemWriteD;
  //   rd = RegDstD; rw = RegWriteD
endmodule
