// Digital circuit PipelinedRegD.dig as structural Verilog
module PipelinedRegD (
  input  clk,
  input  [31:0] InstrF,
  input  [31:0] PCPlus4F,
  input  clr,
  input  NotEN,
  output [31:0] InstrD,
  output [31:0] PCPlus4D
);

  wire en;
  wire [31:0] pulldown_1_out, pulldown_2_out;

  not not_1 (en, NotEN);
  PullDown #(.Bits(32)) pulldown_1 (.out(pulldown_1_out));
  assign pulldown_1_out = ~clr ? InstrF : 32'bz;  // DriverInvSel driverinvsel_1
  PullDown #(.Bits(32)) pulldown_2 (.out(pulldown_2_out));
  assign pulldown_2_out = ~clr ? PCPlus4F : 32'bz;  // DriverInvSel driverinvsel_2
  Register #(.Bits(32)) register_1 (.D(pulldown_1_out), .C(clk), .en(en), .Q(InstrD));
  Register #(.Bits(32)) register_2 (.D(pulldown_2_out), .C(clk), .en(en), .Q(PCPlus4D));
endmodule
