// Digital circuit PipelinedRegE.dig as structural Verilog
module PipelinedRegE (
  input  clk,
  input  RegWriteD,
  input  MemtoRegD,
  input  MemWriteD,
  input  [2:0] ALUControlD,
  input  ALUSrcD,
  input  RegDstD,
  input  [31:0] DaD,
  input  [31:0] DbD,
  input  [4:0] rsD,
  input  [4:0] rtD,
  input  [4:0] rdD,
  input  [31:0] SignImmD,
  input  clr,
  output RegWriteE,
  output MemtoRegE,
  output MemWriteE,
  output [2:0] ALUControlE,
  output ALUSrcE,
  output RegDstE,
  output [31:0] DaE,
  output [31:0] DbE,
  output [4:0] rsE,
  output [4:0] rtE,
  output [4:0] rdE,
  output [31:0] SignImmE
);

  wire driverinvsel_1_out, driverinvsel_2_out, driverinvsel_3_out, driverinvsel_5_out, driverinvsel_6_out;
  wire [2:0] driverinvsel_4_out;
  wire [4:0] driverinvsel_9_out, driverinvsel_10_out, driverinvsel_11_out;
  wire [31:0] driverinvsel_7_out, driverinvsel_8_out, driverinvsel_12_out;

  assign driverinvsel_1_out = ~clr ? RegWriteD : 1'bz;  // DriverInvSel driverinvsel_1
  assign driverinvsel_2_out = ~clr ? MemtoRegD : 1'bz;  // DriverInvSel driverinvsel_2
  assign driverinvsel_3_out = ~clr ? MemWriteD : 1'bz;  // DriverInvSel driverinvsel_3
  assign driverinvsel_4_out = ~clr ? ALUControlD : 3'bz;  // DriverInvSel driverinvsel_4
  assign driverinvsel_5_out = ~clr ? ALUSrcD : 1'bz;  // DriverInvSel driverinvsel_5
  assign driverinvsel_6_out = ~clr ? RegDstD : 1'bz;  // DriverInvSel driverinvsel_6
  assign driverinvsel_7_out = ~clr ? DaD : 32'bz;  // DriverInvSel driverinvsel_7
  assign driverinvsel_8_out = ~clr ? DbD : 32'bz;  // DriverInvSel driverinvsel_8
  assign driverinvsel_9_out = ~clr ? rsD : 5'bz;  // DriverInvSel driverinvsel_9
  assign driverinvsel_10_out = ~clr ? rtD : 5'bz;  // DriverInvSel driverinvsel_10
  assign driverinvsel_11_out = ~clr ? rdD : 5'bz;  // DriverInvSel driverinvsel_11
  assign driverinvsel_12_out = ~clr ? SignImmD : 32'bz;  // DriverInvSel driverinvsel_12
  PullDown pulldown_1 (.out(driverinvsel_1_out));
  PullDown pulldown_2 (.out(driverinvsel_2_out));
  PullDown pulldown_3 (.out(driverinvsel_3_out));
  PullDown #(.Bits(3)) pulldown_4 (.out(driverinvsel_4_out));
  PullDown pulldown_5 (.out(driverinvsel_5_out));
  PullDown pulldown_6 (.out(driverinvsel_6_out));
  PullDown #(.Bits(32)) pulldown_7 (.out(driverinvsel_7_out));
  PullDown #(.Bits(32)) pulldown_8 (.out(driverinvsel_8_out));
  PullDown #(.Bits(5)) pulldown_9 (.out(driverinvsel_9_out));
  PullDown #(.Bits(5)) pulldown_10 (.out(driverinvsel_10_out));
  PullDown #(.Bits(5)) pulldown_11 (.out(driverinvsel_11_out));
  PullDown #(.Bits(32)) pulldown_12 (.out(driverinvsel_12_out));
  Register register_1 (.D(driverinvsel_1_out), .C(clk), .en(1'b1), .Q(RegWriteE));
  Register register_2 (.D(driverinvsel_2_out), .C(clk), .en(1'b1), .Q(MemtoRegE));
  Register register_3 (.D(driverinvsel_3_out), .C(clk), .en(1'b1), .Q(MemWriteE));
  Register #(.Bits(3)) register_4 (.D(driverinvsel_4_out), .C(clk), .en(1'b1), .Q(ALUControlE));
  Register register_5 (.D(driverinvsel_5_out), .C(clk), .en(1'b1), .Q(ALUSrcE));
  Register register_6 (.D(driverinvsel_6_out), .C(clk), .en(1'b1), .Q(RegDstE));
  Register #(.Bits(32)) register_7 (.D(driverinvsel_7_out), .C(clk), .en(1'b1), .Q(DaE));
  Register #(.Bits(32)) register_8 (.D(driverinvsel_8_out), .C(clk), .en(1'b1), .Q(DbE));
  Register #(.Bits(5)) register_9 (.D(driverinvsel_9_out), .C(clk), .en(1'b1), .Q(rsE));
  Register #(.Bits(5)) register_10 (.D(driverinvsel_10_out), .C(clk), .en(1'b1), .Q(rtE));
  Register #(.Bits(5)) register_11 (.D(driverinvsel_11_out), .C(clk), .en(1'b1), .Q(rdE));
  Register #(.Bits(32)) register_12 (.D(driverinvsel_12_out), .C(clk), .en(1'b1), .Q(SignImmE));
endmodule
