// Digital circuit PipelinedRegM.dig as structural Verilog
module PipelinedRegM (
  input  clk,
  input  RegWriteE,
  input  MemtoRegE,
  input  MemWriteE,
  input  [31:0] ALUOutE,
  input  [31:0] WriteDataE,
  input  [4:0] WriteRegE,
  output RegWriteM,
  output MemtoRegM,
  output MemWriteM,
  output [31:0] ALUOutM,
  output [31:0] WriteDataM,
  output [4:0] WriteRegM
);

  wire driverinvsel_1_out, driverinvsel_2_out, driverinvsel_3_out;
  wire [4:0] driverinvsel_6_out;
  wire [31:0] driverinvsel_4_out, driverinvsel_5_out;

  assign driverinvsel_1_out = ~1'b0 ? RegWriteE : 1'bz;  // DriverInvSel driverinvsel_1
  assign driverinvsel_2_out = ~1'b0 ? MemtoRegE : 1'bz;  // DriverInvSel driverinvsel_2
  assign driverinvsel_3_out = ~1'b0 ? MemWriteE : 1'bz;  // DriverInvSel driverinvsel_3
  assign driverinvsel_4_out = ~1'b0 ? ALUOutE : 32'bz;  // DriverInvSel driverinvsel_4
  assign driverinvsel_5_out = ~1'b0 ? WriteDataE : 32'bz;  // DriverInvSel driverinvsel_5
  assign driverinvsel_6_out = ~1'b0 ? WriteRegE : 5'bz;  // DriverInvSel driverinvsel_6
  PullDown pulldown_1 (.out(driverinvsel_1_out));
  PullDown pulldown_2 (.out(driverinvsel_2_out));
  PullDown pulldown_3 (.out(driverinvsel_3_out));
  PullDown #(.Bits(32)) pulldown_4 (.out(driverinvsel_4_out));
  PullDown #(.Bits(32)) pulldown_5 (.out(driverinvsel_5_out));
  PullDown #(.Bits(5)) pulldown_6 (.out(driverinvsel_6_out));
  Register register_1 (.D(driverinvsel_1_out), .C(clk), .en(1'b1), .Q(RegWriteM));
  Register register_2 (.D(driverinvsel_2_out), .C(clk), .en(1'b1), .Q(MemtoRegM));
  Register register_3 (.D(driverinvsel_3_out), .C(clk), .en(1'b1), .Q(MemWriteM));
  Register #(.Bits(32)) register_4 (.D(driverinvsel_4_out), .C(clk), .en(1'b1), .Q(ALUOutM));
  Register #(.Bits(32)) register_5 (.D(driverinvsel_5_out), .C(clk), .en(1'b1), .Q(WriteDataM));
  Register #(.Bits(5)) register_6 (.D(driverinvsel_6_out), .C(clk), .en(1'b1), .Q(WriteRegM));
endmodule
