// Digital circuit PipelinedRegW.dig as structural Verilog
module PipelinedRegW (
  input  clk,
  input  RegWriteM,
  input  MemtoRegM,
  input  [31:0] ReadDataM,
  input  [31:0] ALUOutM,
  input  [4:0] WriteRegM,
  output RegWriteW,
  output MemtoRegW,
  output [31:0] ReadDataW,
  output [31:0] ALUOutW,
  output [4:0] WriteRegW
);

  wire pulldown_1_out, pulldown_2_out;
  wire [4:0] pulldown_5_out;
  wire [31:0] pulldown_3_out, pulldown_4_out;

  PullDown pulldown_1 (.out(pulldown_1_out));
  assign pulldown_1_out = ~1'b0 ? RegWriteM : 1'bz;  // DriverInvSel driverinvsel_1
  PullDown pulldown_2 (.out(pulldown_2_out));
  assign pulldown_2_out = ~1'b0 ? MemtoRegM : 1'bz;  // DriverInvSel driverinvsel_2
  PullDown #(.Bits(32)) pulldown_3 (.out(pulldown_3_out));
  assign pulldown_3_out = ~1'b0 ? ReadDataM : 32'bz;  // DriverInvSel driverinvsel_3
  PullDown #(.Bits(32)) pulldown_4 (.out(pulldown_4_out));
  assign pulldown_4_out = ~1'b0 ? ALUOutM : 32'bz;  // DriverInvSel driverinvsel_4
  PullDown #(.Bits(5)) pulldown_5 (.out(pulldown_5_out));
  assign pulldown_5_out = ~1'b0 ? WriteRegM : 5'bz;  // DriverInvSel driverinvsel_5
  Register register_1 (.D(pulldown_1_out), .C(clk), .en(1'b1), .Q(RegWriteW));
  Register register_2 (.D(pulldown_2_out), .C(clk), .en(1'b1), .Q(MemtoRegW));
  Register #(.Bits(32)) register_3 (.D(pulldown_3_out), .C(clk), .en(1'b1), .Q(ReadDataW));
  Register #(.Bits(32)) register_4 (.D(pulldown_4_out), .C(clk), .en(1'b1), .Q(ALUOutW));
  Register #(.Bits(5)) register_5 (.D(pulldown_5_out), .C(clk), .en(1'b1), .Q(WriteRegW));
endmodule
