// Digital circuit PipelinedProcessor.dig as structural Verilog
module PipelinedProcessor (
  input  clk
);

  wire ALUSrcD, BranchD, comparator_1_eq, FlushE, ForwardAD, ForwardBD, JumpD, MemtoRegD, MemtoRegE,
       MemtoRegM, MemWriteD, MemWriteE, not_1_out, not_2_out, or_1_out, PCSrcD, pipelinedrege_1_alusrce,
       pipelinedrege_1_regdste, pipelinedregm_1_memwritem, pipelinedregw_1_memtoregw, RegDstD, RegWriteD,
       RegWriteE, RegWriteM, RegWriteW, StallD, StallF;
  wire [1:0] ForwardAE, ForwardBE;
  wire [2:0] ALUControlD, pipelinedrege_1_alucontrole;
  wire [4:0] I10_6, I20_16, pipelinedrege_1_rde, rsE, rtE, WriteRegE, WriteRegM, WriteRegW;
  wire [5:0] I5_0, I31_26;
  wire [15:11] I15_0;
  wire [25:21] I25_0;
  wire [27:0] PCPlus4D;
  wire [31:0] add_1_s, alu_1_y, ALUOutM, barrelshifter_1_out, bitextender_1_out, DataMemory_d, div_1_q,
       div_2_q, InstructionMemory_d, multiplexer_1_out, multiplexer_2_out, multiplexer_3_out,
       multiplexer_4_out, multiplexer_6_out, multiplexer_7_out, multiplexer_8_out, PC_q, PCBranchD,
       pipelinedrege_1_dae, pipelinedrege_1_dbe, pipelinedrege_1_signimme, pipelinedregm_1_writedatam,
       pipelinedregw_1_aluoutw, pipelinedregw_1_readdataw, registerfile_1_da, registerfile_1_db, ResultW;
  wire [31:28] PCJumpD;

  Multiplexer #(.Bits(32)) multiplexer_1 (.sel(PCSrcD), .in_0(add_1_s), .in_1(PCBranchD), .out(multiplexer_1_out));
  Multiplexer #(.Bits(32)) multiplexer_2 (
    .sel(JumpD), .in_0(multiplexer_1_out), .in_1({PCJumpD, I25_0, I20_16, I15_0, I10_6, I5_0, 2'b00}),
    .out(multiplexer_2_out));
  Register #(.Bits(32)) PC (.D(multiplexer_2_out), .C(clk), .en(not_1_out), .Q(PC_q));
  not not_1 (not_1_out, StallF);
  // Probe on PC_q
  Div #(.Bits(32)) div_1 (.a(PC_q), .b(32'h4), .q(div_1_q));  // open: r
  Add #(.Bits(32)) add_1 (.a(PC_q), .b(32'h4), .c_i(1'b0), .s(add_1_s));  // open: c_o
  ROM #(.AddrBits(16), .Bits(32)) InstructionMemory (.A(div_1_q[15:0]), .sel(1'b1), .D(InstructionMemory_d));
  or or_1 (or_1_out, PCSrcD, JumpD);
  PipelinedRegD pipelinedregd_1 (
    .clk(clk), .InstrF(InstructionMemory_d), .PCPlus4F(add_1_s), .clr(or_1_out), .NotEN(StallD),
    .InstrD({I31_26, I25_0, I20_16, I15_0, I10_6, I5_0}), .PCPlus4D({PCJumpD, PCPlus4D}));
  // Probe on {I31_26, I25_0, I20_16, I15_0, I10_6, I5_0}
  PipelinedControlUnit pipelinedcontrolunit_1 (
    .Op(I31_26), .Funct(I5_0), .RegWriteD(RegWriteD), .MemtoRegD(MemtoRegD), .MemWriteD(MemWriteD),
    .ALUControlD(ALUControlD), .ALUSrcD(ALUSrcD), .RegDstD(RegDstD), .BranchD(BranchD), .JumpD(JumpD));
  not not_2 (not_2_out, clk);
  HazardUnit hazardunit_1 (
    .rsD(I25_0), .rtD(I20_16), .rsE(rsE), .rtE(rtE), .WriteRegE(WriteRegE), .WriteRegM(WriteRegM),
    .WriteRegW(WriteRegW), .BranchD(BranchD), .RegWriteE(RegWriteE), .MemtoRegE(MemtoRegE),
    .RegWriteM(RegWriteM), .MemtoRegM(MemtoRegM), .RegWriteW(RegWriteW), .ForwardAD(ForwardAD),
    .ForwardBD(ForwardBD), .ForwardAE(ForwardAE), .ForwardBE(ForwardBE), .StallF(StallF), .StallD(StallD),
    .FlushE(FlushE));
  RegisterFile #(.AddrBits(5), .Bits(32)) registerfile_1 (
    .Din(ResultW), .we(RegWriteW), .Rw(WriteRegW), .C(not_2_out), .Ra(I25_0), .Rb(I20_16),
    .Da(registerfile_1_da), .Db(registerfile_1_db));
  BitExtender #(.inputBits(16), .outputBits(32)) bitextender_1 (.in({I15_0, I10_6, I5_0}), .out(bitextender_1_out));
  BarrelShifter #(.Bits(32)) barrelshifter_1 (.in(bitextender_1_out), .shift(6'b000010), .out(barrelshifter_1_out));
  Multiplexer #(.Bits(32)) multiplexer_3 (
    .sel(ForwardAD), .in_0(registerfile_1_da), .in_1(ALUOutM), .out(multiplexer_3_out));
  Multiplexer #(.Bits(32)) multiplexer_4 (
    .sel(ForwardBD), .in_0(registerfile_1_db), .in_1(ALUOutM), .out(multiplexer_4_out));
  Comparator #(.Bits(32)) comparator_1 (
    .a(multiplexer_3_out), .b(multiplexer_4_out), .eq(comparator_1_eq));  // open: gt, lt
  Add #(.Bits(32)) add_2 (.a(barrelshifter_1_out), .b({PCJumpD, PCPlus4D}), .c_i(1'b0), .s(PCBranchD));  // open: c_o
  and and_1 (PCSrcD, BranchD, comparator_1_eq);
  PipelinedRegE pipelinedrege_1 (
    .clk(clk), .RegWriteD(RegWriteD), .MemtoRegD(MemtoRegD), .MemWriteD(MemWriteD),
    .ALUControlD(ALUControlD), .ALUSrcD(ALUSrcD), .RegDstD(RegDstD), .DaD(multiplexer_3_out),
    .DbD(multiplexer_4_out), .rsD(I25_0), .rtD(I20_16), .rdD(I15_0), .SignImmD(bitextender_1_out),
    .clr(FlushE), .RegWriteE(RegWriteE), .MemtoRegE(MemtoRegE), .MemWriteE(MemWriteE),
    .ALUControlE(pipelinedrege_1_alucontrole), .ALUSrcE(pipelinedrege_1_alusrce),
    .RegDstE(pipelinedrege_1_regdste), .DaE(pipelinedrege_1_dae), .DbE(pipelinedrege_1_dbe), .rsE(rsE),
    .rtE(rtE), .rdE(pipelinedrege_1_rde), .SignImmE(pipelinedrege_1_signimme));
  Multiplexer #(.Bits(5)) multiplexer_5 (
    .sel(pipelinedrege_1_regdste), .in_0(rtE), .in_1(pipelinedrege_1_rde), .out(WriteRegE));
  Multiplexer #(.Selector_Bits(2), .Bits(32)) multiplexer_6 (
    .sel(ForwardAE), .in_0(pipelinedrege_1_dae), .in_1(ResultW), .in_2(ALUOutM), .in_3({32{1'b0}}),
    .out(multiplexer_6_out));
  Multiplexer #(.Selector_Bits(2), .Bits(32)) multiplexer_7 (
    .sel(ForwardBE), .in_0(pipelinedrege_1_dbe), .in_1(ResultW), .in_2(ALUOutM), .in_3({32{1'b0}}),
    .out(multiplexer_7_out));
  Multiplexer #(.Bits(32)) multiplexer_8 (
    .sel(pipelinedrege_1_alusrce), .in_0(multiplexer_7_out), .in_1(pipelinedrege_1_signimme),
    .out(multiplexer_8_out));
  ALU alu_1 (.F(pipelinedrege_1_alucontrole), .A(multiplexer_6_out), .B(multiplexer_8_out), .Y(alu_1_y));  // open: _0
  PipelinedRegM pipelinedregm_1 (
    .clk(clk), .RegWriteE(RegWriteE), .MemtoRegE(MemtoRegE), .MemWriteE(MemWriteE), .ALUOutE(alu_1_y),
    .WriteDataE(multiplexer_7_out), .WriteRegE(WriteRegE), .RegWriteM(RegWriteM), .MemtoRegM(MemtoRegM),
    .MemWriteM(pipelinedregm_1_memwritem), .ALUOutM(ALUOutM), .WriteDataM(pipelinedregm_1_writedatam),
    .WriteRegM(WriteRegM));
  Div #(.Bits(32)) div_2 (.a(ALUOutM), .b(32'h4), .q(div_2_q));  // open: r
  EEPROMDualPort #(.AddrBits(16), .Bits(32)) DataMemory (
    .A(div_2_q[15:0]), .Din(pipelinedregm_1_writedatam), .str(pipelinedregm_1_memwritem), .C(clk), .ld(1'b1),
    .D(DataMemory_d));
  PipelinedRegW pipelinedregw_1 (
    .clk(clk), .RegWriteM(RegWriteM), .MemtoRegM(MemtoRegM), .ReadDataM(DataMemory_d), .ALUOutM(ALUOutM),
    .WriteRegM(WriteRegM), .RegWriteW(RegWriteW), .MemtoRegW(pipelinedregw_1_memtoregw),
    .ReadDataW(pipelinedregw_1_readdataw), .ALUOutW(pipelinedregw_1_aluoutw), .WriteRegW(WriteRegW));
  Multiplexer #(.Bits(32)) multiplexer_9 (
    .sel(pipelinedregw_1_memtoregw), .in_0(pipelinedregw_1_aluoutw), .in_1(pipelinedregw_1_readdataw),
    .out(ResultW));

  // Other names for the same wires on the sheet: I15_0[10:0] = {I10_6, I5_0};
  //   I25_0[20:0] = {I20_16, I15_0, I10_6, I5_0}; PCJumpD[27:2] = {I25_0, I20_16, I15_0, I10_6, I5_0};
  //   I15_11[4:0] = I15_0; I25_21[4:0] = I25_0; PCPlus4D[31:28] = PCJumpD

  // Notes on the sheet:
  //   clk: Hz: 10
  //   contents of InstructionMemory (hex, n*v repeats v):
  //   ac000064,ac000068,20020005,2003000c,2067fff7,e22025,642824,a42820,10a7000a,64202a,
  //   10800001,20050000,e2202a,853820,e23822,ac670058,8c020064,8000013,20020001,ac020068,
  //   8000014
  //   funct 5:0
  //   shamt 10:6
  //   rd 15:11
  //   rt 20:16
  //   rs 25:21
  //   op 31:26
endmodule
