// Digital circuit SingleCycleControlUnit.dig as structural Verilog
module SingleCycleControlUnit (
  input  [5:0] Op,
  input  [5:0] Funct,
  output MemtoReg,
  output MemWrite,
  output Branch,
  output [2:0] ALUControl,
  output ALUSrc,
  output RegDst,
  output RegWrite,
  output Jump
);

  wire [1:0] singlecyclemaindecoder_1_aluop;

  SingleCycleMainDecoder singlecyclemaindecoder_1 (
    .Op(Op), .MemtoReg(MemtoReg), .MemWrite(MemWrite), .Branch(Branch), .ALUSrc(ALUSrc), .RegDst(RegDst),
    .RegWrite(RegWrite), .Jump(Jump), .ALUOp(singlecyclemaindecoder_1_aluop));
  ALUDecoder aludecoder_1 (.ALUOp(singlecyclemaindecoder_1_aluop), .Funct(Funct), .ALUControl(ALUControl));

  // Other names for the same wires on the sheet: as = ALUSrc; b = Branch; j = Jump; mr = MemtoReg; mw = MemWrite;
  //   rd = RegDst; rw = RegWrite
endmodule
