// Digital circuit SingleCycleMainDecoder.dig as structural Verilog
module SingleCycleMainDecoder (
  input  [5:0] Op,
  output MemtoReg,
  output MemWrite,
  output Branch,
  output ALUSrc,
  output RegDst,
  output RegWrite,
  output Jump,
  output [1:0] ALUOp
);

  wire and_1_out, and_2_out, and_3_out, and_5_out, and_6_out, and_7_out, not_1_out, not_2_out, not_3_out,
       not_4_out, not_5_out, not_6_out;

  not not_1 (not_1_out, Op[0]);
  not not_2 (not_2_out, Op[1]);
  not not_3 (not_3_out, Op[2]);
  not not_4 (not_4_out, Op[3]);
  not not_5 (not_5_out, Op[4]);
  not not_6 (not_6_out, Op[5]);
  and and_1 (and_1_out, not_1_out, not_2_out, not_3_out, not_4_out, not_5_out, not_6_out);
  and and_2 (and_2_out, Op[0], Op[1], not_3_out, not_4_out, not_5_out, Op[5]);
  and and_3 (and_3_out, not_1_out, not_2_out, not_3_out, Op[3], not_5_out, not_6_out);
  and and_4 (RegDst, not_1_out, not_2_out, not_3_out, not_4_out, not_5_out, not_6_out);
  and and_5 (and_5_out, Op[0], Op[1], not_3_out, not_4_out, not_5_out, Op[5]);
  and and_6 (and_6_out, Op[0], Op[1], not_3_out, Op[3], not_5_out, Op[5]);
  and and_7 (and_7_out, not_1_out, not_2_out, not_3_out, Op[3], not_5_out, not_6_out);
  and and_8 (Branch, not_1_out, not_2_out, Op[2], not_4_out, not_5_out, not_6_out);
  and and_9 (MemWrite, Op[0], Op[1], not_3_out, Op[3], not_5_out, Op[5]);
  and and_10 (MemtoReg, Op[0], Op[1], not_3_out, not_4_out, not_5_out, Op[5]);
  and and_11 (ALUOp[1], not_1_out, not_2_out, not_3_out, not_4_out, not_5_out, not_6_out);
  and and_12 (ALUOp[0], not_1_out, not_2_out, Op[2], not_4_out, not_5_out, not_6_out);
  and and_13 (Jump, not_1_out, Op[1], not_3_out, not_4_out, not_5_out, not_6_out);
  or or_1 (RegWrite, and_1_out, and_2_out, and_3_out);
  or or_2 (ALUSrc, and_5_out, and_6_out, and_7_out);

  // Other names for the same wires on the sheet: o0 = Op[0]; o1 = Op[1]; o2 = Op[2]; o3 = Op[3]; o4 = Op[4];
  //   o5 = Op[5]
endmodule
