// Digital circuit SingleCycleProcessor.dig as structural Verilog
module SingleCycleProcessor (
  input  clk
);

  wire alu_1__0, ALUSrc, Branch, Jump, MemtoReg, MemWrite, PCSrc, RegDst, RegWrite;
  wire [2:0] ALUControl;
  wire [4:0] I10_6, I20_16, multiplexer_3_out;
  wire [5:0] I5_0, I31_26;
  wire [15:11] I15_0;
  wire [25:21] I25_0;
  wire [31:0] alu_1_y, barrelshifter_1_out, bitextender_1_out, DataMemory_d, div_1_q, div_2_q,
       multiplexer_1_out, multiplexer_2_out, multiplexer_4_out, PC_q, PCBranch, PCPlus4, registerfile_1_da,
       registerfile_1_db, Result;

  Multiplexer #(.Bits(32)) multiplexer_1 (.sel(PCSrc), .in_0(PCPlus4), .in_1(PCBranch), .out(multiplexer_1_out));
  Multiplexer #(.Bits(32)) multiplexer_2 (
    .sel(Jump), .in_0(multiplexer_1_out), .in_1({PCPlus4[31:28], I25_0, I20_16, I15_0, I10_6, I5_0, 2'b00}),
    .out(multiplexer_2_out));
  Register #(.Bits(32)) PC (.D(multiplexer_2_out), .C(clk), .en(1'b1), .Q(PC_q));
  // Probe on PC_q
  Div #(.Bits(32)) div_1 (.a(PC_q), .b(32'h4), .q(div_1_q));  // open: r
  Add #(.Bits(32)) add_1 (.a(PC_q), .b(32'h4), .c_i(1'b0), .s(PCPlus4));  // open: c_o
  SingleCycleControlUnit singlecyclecontrolunit_1 (
    .Op(I31_26), .Funct(I5_0), .MemtoReg(MemtoReg), .MemWrite(MemWrite), .Branch(Branch),
    .ALUControl(ALUControl), .ALUSrc(ALUSrc), .RegDst(RegDst), .RegWrite(RegWrite), .Jump(Jump));
  // Probe on {I31_26, I25_0, I20_16, I15_0, I10_6, I5_0}
  ROM #(.AddrBits(16), .Bits(32)) InstructionMemory (
    .A(div_1_q[15:0]), .sel(1'b1), .D({I31_26, I25_0, I20_16, I15_0, I10_6, I5_0}));
  Multiplexer #(.Bits(5)) multiplexer_3 (.sel(RegDst), .in_0(I20_16), .in_1(I15_0), .out(multiplexer_3_out));
  BitExtender #(.inputBits(16), .outputBits(32)) bitextender_1 (.in({I15_0, I10_6, I5_0}), .out(bitextender_1_out));
  RegisterFile #(.AddrBits(5), .Bits(32)) registerfile_1 (
    .Din(Result), .we(RegWrite), .Rw(multiplexer_3_out), .C(clk), .Ra(I25_0), .Rb(I20_16),
    .Da(registerfile_1_da), .Db(registerfile_1_db));
  BarrelShifter #(.Bits(32)) barrelshifter_1 (.in(bitextender_1_out), .shift(6'b000010), .out(barrelshifter_1_out));
  Multiplexer #(.Bits(32)) multiplexer_4 (
    .sel(ALUSrc), .in_0(registerfile_1_db), .in_1(bitextender_1_out), .out(multiplexer_4_out));
  Add #(.Bits(32)) add_2 (.a(barrelshifter_1_out), .b(PCPlus4), .c_i(1'b0), .s(PCBranch));  // open: c_o
  ALU alu_1 (.F(ALUControl), .A(registerfile_1_da), .B(multiplexer_4_out), ._0(alu_1__0), .Y(alu_1_y));
  and and_1 (PCSrc, Branch, alu_1__0);
  Div #(.Bits(32)) div_2 (.a(alu_1_y), .b(32'h4), .q(div_2_q));  // open: r
  EEPROMDualPort #(.AddrBits(16), .Bits(32)) DataMemory (
    .A(div_2_q[15:0]), .Din(registerfile_1_db), .str(MemWrite), .C(clk), .ld(1'b1), .D(DataMemory_d));
  Multiplexer #(.Bits(32)) multiplexer_5 (.sel(MemtoReg), .in_0(alu_1_y), .in_1(DataMemory_d), .out(Result));

  // Other names for the same wires on the sheet: I15_0[10:0] = {I10_6, I5_0};
  //   I25_0[20:0] = {I20_16, I15_0, I10_6, I5_0}; I15_11[4:0] = I15_0; I25_21[4:0] = I25_0

  // Notes on the sheet:
  //   clk: Hz: 10
  //   contents of InstructionMemory (hex, n*v repeats v):
  //   ac000064,ac000068,20020005,2003000c,2067fff7,e22025,642824,a42820,10a7000a,64202a,
  //   10800001,20050000,e2202a,853820,e23822,ac670058,8c020064,8000013,20020001,ac020068,
  //   8000014
  //   funct 5:0
  //   shamt 10:6
  //   rd 15:11
  //   rt 20:16
  //   rs 25:21
  //   op 31:26
endmodule
